// Digital circuit regfile.dig as structural Verilog
module regfile (
  input  clk,
  input  rst,
  input  [31:0] wdata,
  input  [4:0] waddr,
  input  we,
  input  [4:0] raddr1,
  input  re1,
  input  [4:0] raddr2,
  input  re2,
  output [31:0] rdata1,
  output [31:0] rdata2
);

  wire and_1_out, and_2_out, and_3_out, comparator_1_gt, comparator_2_gt, comparator_3_gt, not_1_out;

  Comparator #(.Bits(5)) comparator_1 (.a(raddr2), .b({5{1'b0}}), .gt(comparator_1_gt));  // open: eq, lt
  and and_1 (and_1_out, not_1_out, re2, comparator_1_gt);
  Comparator #(.Bits(5)) comparator_2 (.a(raddr1), .b({5{1'b0}}), .gt(comparator_2_gt));  // open: eq, lt
  and and_2 (and_2_out, not_1_out, re1, comparator_2_gt);
  Comparator #(.Bits(5)) comparator_3 (.a(waddr), .b({5{1'b0}}), .gt(comparator_3_gt));  // open: eq, lt
  and and_3 (and_3_out, not_1_out, we, comparator_3_gt);
  not not_1 (not_1_out, rst);
  reg_32 reg_32_1 (
    .clk(clk), .we(and_3_out), .waddr(waddr), .wdata(wdata), .re1(and_2_out), .raddr1(raddr1),
    .re2(and_1_out), .raddr2(raddr2), .A_1(rdata1), .A_2(rdata2));

  // Notes on the sheet:
  //   rst: 復位信號
  //   wdata: 要寫入的數據
  //   rdata1: 第一個讀取暫存器連接埠輸出的暫存器值
  //   rdata2: 第二個讀取暫存器連接埠輸出的暫存器值
  //   waddr: 要寫入的暫存器地址
  //   we: 寫入啟用訊號
  //   raddr1: 第一個讀取暫存器埠要讀取的暫存器的位址
  //   re1: 第一個讀取暫存器埠讀啟用訊號
  //   raddr2: 第一個讀取暫存器埠要讀取的暫存器的位址
  //   re2: 第一個讀取暫存器埠讀啟用訊號
endmodule
